// Logisim project bool-ex8-logick.circ as structural Verilog: 1 circuit, main circuit main
module main (
  input  A,
  input  B,
  input  C,
  input  D,
  output LED1,
  output out_6,
  output out_7
);

  wire and_1_out, and_2_out, or_1_out;

  and and_1 (and_1_out, A, ~B, ~C);  // AND_Gate
  and and_2 (and_2_out, ~A, B);  // AND_Gate
  or or_1 (or_1_out, B, C);
  and and_3 (LED1, ~A, ~B);  // AND_Gate
  or or_2 (out_6, and_1_out, and_2_out);
  and and_4 (out_7, A, or_1_out);
endmodule
