// Logisim project decoder.circ as structural Verilog: 1 circuit, main circuit main
module main (
  input  A0,
  input  A1,
  output out_3,
  output out_4,
  output out_5,
  output out_6
);

  wire not_1_out, not_2_out;

  not not_1 (not_1_out, A0);
  not not_2 (not_2_out, A1);
  and Y0 (out_3, not_1_out, not_2_out);
  and Y1 (out_4, A0, not_2_out);
  and Y2 (out_5, not_1_out, A1);
  and Y3 (out_6, A0, A1);
endmodule
