// Logisim project encoder.circ as structural Verilog: 1 circuit, main circuit main
module main (
  input  A3,
  input  A2,
  input  A1,
  input  A0,
  output out_5,
  output out_6
);

  or Y1 (out_5, A3, A2);
  or Y0 (out_6, A3, A1);
endmodule
