// Logisim project mux.circ as structural Verilog: 1 circuit, main circuit main
module main (
  input  A1,
  input  A0,
  input  in_3
);

  wire and_1_out, and_2_out, not_1_out, or_1_out;

  and and_1 (and_1_out, A1, in_3);
  and and_2 (and_2_out, A0, not_1_out);
  not not_1 (not_1_out, in_3);
  or or_1 (or_1_out, and_1_out, and_2_out);
endmodule
