// Logisim project 4-1-demux.circ as structural Verilog: 1 circuit, main circuit main
module main (
  input  in_1,
  input  [1:0] in_2,
  input  b,
  input  a,
  input  in_5,
  output out_6,
  output out_7,
  output out_8,
  output out_9,
  output out_10,
  output out_11,
  output out_12,
  output out_13
);

  wire not_1_out, not_2_out;

  Demultiplexer #(.select(2), .enable("false")) demultiplexer_1 (
    .out0(out_6), .out1(out_7), .out2(out_8), .out3(out_9), .in(in_1), .sel(in_2));
  not not_1 (not_1_out, b);
  not not_2 (not_2_out, a);
  and and_1 (out_10, in_5, not_2_out, not_1_out);
  and and_2 (out_11, in_5, a, not_1_out);
  and and_3 (out_12, in_5, not_2_out, b);
  and and_4 (out_13, in_5, a, b);
endmodule
