// Logisim project lesson-ex2-problems1.circ as structural Verilog: 1 circuit, main circuit main
module main (
  input  in_1,
  input  in_2,
  input  in_3,
  input  in_4,
  input  in_5,
  input  in_6,
  input  in_7,
  input  in_8,
  input  in_9,
  output out_10,
  output out_11,
  output out_12
);

  wire and_1_out, and_2_out, or_1_out, or_2_out, or_3_out, or_4_out, or_5_out, or_6_out;

  or or_1 (or_1_out, ~in_1, in_2);  // OR_Gate
  or or_2 (or_2_out, in_1, ~in_2);  // OR_Gate
  or or_3 (or_3_out, in_1, in_3);
  and and_1 (and_1_out, in_4, in_5);
  and and_2 (and_2_out, ~in_4, ~in_5, in_6);  // AND_Gate
  or or_4 (or_4_out, ~in_7, in_8);  // OR_Gate
  or or_5 (or_5_out, in_7, ~in_8);  // OR_Gate
  or or_6 (or_6_out, ~in_7, ~in_9);  // OR_Gate
  and and_3 (out_10, or_1_out, or_2_out, or_3_out);
  or or_7 (out_11, and_1_out, and_2_out);
  and and_4 (out_12, ~or_4_out, ~or_5_out, ~or_6_out);  // AND_Gate
endmodule
