// Logisim project lesson-ex2-problems3.circ as structural Verilog: 1 circuit, main circuit main
module main (
  input  in_1,
  input  in_2,
  input  in_3,
  output out_4
);

  wire or_1_out, or_2_out, or_3_out;

  or or_1 (or_1_out, ~in_1, in_2);  // OR_Gate
  or or_2 (or_2_out, in_1, ~in_2);  // OR_Gate
  or or_3 (or_3_out, ~in_1, ~in_3);  // OR_Gate
  and and_1 (out_4, ~or_1_out, ~or_2_out, ~or_3_out);  // AND_Gate
endmodule
