// Logisim project lesson-ex3-b-mux.circ as structural Verilog: 1 circuit, main circuit main
module main (
  input  in_1,
  input  in_2,
  input  [3:0] in_3,
  output out_4
);

  Multiplexer #(.select(3), .enable("false")) multiplexer_1 (.out(out_4));  // open: in0, in1, in2, in3, in4, in5, in6, in7, sel
endmodule
