// Logisim project 4-1-mux.circ as structural Verilog: 1 circuit, main circuit main
module main (
  input  D,
  input  in_2,
  input  in_3,
  input  C,
  input  in_5,
  input  B,
  input  in_7,
  input  A,
  input  [1:0] in_9,
  input  b_2,
  input  D_2,
  input  a_2,
  input  C_2,
  input  B_3,
  input  A_3,
  input  b_4,
  input  a_4,
  output out_18,
  output out_19,
  output out_20
);

  wire and_1_out, and_2_out, and_3_out, and_4_out, nand_1_out, nand_2_out, nand_3_out, nand_4_out, not_1_out,
       not_2_out, not_3_out, not_4_out;

  Multiplexer #(.select(2), .enable("false")) multiplexer_1 (
    .in0(in_2), .in1(in_3), .in2(in_5), .in3(in_7), .out(out_18), .sel(in_9));
  not not_1 (not_1_out, b_4);
  not not_2 (not_2_out, a_4);
  nand nand_1 (nand_1_out, D_2, not_2_out, b_4);
  nand nand_2 (nand_2_out, C_2, not_2_out, b_4);
  nand nand_3 (nand_3_out, B_3, a_4, not_1_out);
  nand nand_4 (nand_4_out, A_3, not_2_out, not_1_out);
  not not_3 (not_3_out, b_2);
  not not_4 (not_4_out, a_2);
  nand nand_5 (out_20, nand_1_out, nand_2_out, nand_3_out, nand_4_out);
  and and_1 (and_1_out, D, a_2, b_2);
  and and_2 (and_2_out, C, not_4_out, b_2);
  and and_3 (and_3_out, B, a_2, not_3_out);
  and and_4 (and_4_out, A, not_4_out, not_3_out);
  or or_1 (out_19, and_1_out, and_2_out, and_3_out, and_4_out);
endmodule
