// Logisim project d-flip-flop-from-latches.circ as structural Verilog: 1 circuit, main circuit main
module main (
  input  D,
  input  EN,
  output Q,
  output Out,
  output nQ
);

  wire nand_1_out, nand_2_out, nand_6_out, not_1_out;

  not not_1 (not_1_out, D);
  nand nand_1 (nand_1_out, D, EN);
  nand nand_2 (nand_2_out, EN, not_1_out);
  nand nand_3 (Q, nand_1_out, nQ);
  nand nand_4 (nQ, Q, nand_2_out);
  nand nand_5 (Out, Q, nand_6_out);
  nand nand_6 (nand_6_out, Out, nQ);

  // Notes on the sheet:
  //   Master = D-salpa (D-latch)
  //   With enable (not a clock signal), this is a asynchronous
  //   Slave = SR-salpa (SR-latch)
endmodule
